# Fritzing sketch print-a-tweet_v2.0 (saved by Fritzing 0.7.12b)
breadboards: 1

parts:
  USB = USB connector [package=THT]
  U1 = attiny85 [package=dip]
  Switching = Rectifier Diode [part_number=1N4001 package="300 mil [THT]"]
  Diodes = Rectifier Diode [part_number=1N4001 package="300 mil [THT]"]
  R1 = 1.5k Ω Resistor [package=THT]
  R2 = 68 Ω Resistor [package=THT]
  R4 = 10k Ω Resistor [package=THT]
  1A-5V = Power plug
  Thermal = Thermal Printer
  C2 = Ceramic Capacitor [package=THT]
  C1 = Ceramic Capacitor [package=THT]
  S1 = Tilt Switch [package=THT]
  R3 = 68 Ω Resistor [package=THT]
  J2 = female pin header, 4 pins [form="♀ (female)"]
  J3 = female pin header, 4 pins [form="♀ (female)"]

nets:
  N1: USB.5V, Switching.anode, C1.pin_1
  N2: USB.d-, R1.Pin_1, R2.Pin_1
  N3: USB.d+, R3.Pin_1
  GND: USB.GND, USB.chassis5, USB.chassis6, U1.Pin_4, R4.Pin_1, 1A-5V.GND, Thermal.GND, C2.pin_1, C1.pin_0, J2.pin4
  N4: U1.Pin_1, J2.pin1
  N5: U1.Pin_2, Thermal.TXD, J2.pin2
  N6: U1.Pin_3, Thermal.RXD, J2.pin3
  N7: U1.Pin_5, R3.Pin_0, J3.pin4
  N8: U1.Pin_6, R4.Pin_0, S1.Pin_2, J3.pin3
  N9: U1.Pin_7, R2.Pin_0, J3.pin2
  N10: U1.Pin_8, Diodes.cathode, R1.Pin_0, S1.Pin_1, J3.pin1
  N11: Switching.cathode, Diodes.anode
  N12: 1A-5V.VCC, Thermal.VH, C2.pin_0

notes:
  Print-A-Tweet v2.0
  ------------------
  Falk-Wallace
